// Logisim project adder.circ as structural Verilog: 1 circuit, main circuit main
module main (
  input  in_1,
  input  in_2,
  input  in_3,
  input  [4:0] in_4,
  input  [12:0] in_5,
  input  in_6,
  input  in_7,
  input  in_8,
  input  [4:0] in_9,
  input  [12:0] in_10,
  output [4:0] out_11,
  output [4:0] out_12,
  output [15:0] out_13,
  output [15:0] out_14,
  output [15:0] out_15,
  output [15:0] out_16,
  output [15:0] out_17,
  output Inf,
  output sign,
  output out_20,
  output [4:0] exponent,
  output underflow
);

  wire and_1_out, and_4_out, and_6_out, and_7_out, and_8_out, and_10_out, and_11_out, and_13_out, and_14_out,
       and_15_out, and_31_out, nor_1_out, nor_2_out, nor_6_out, nor_7_out, not_1_out, not_2_out, not_3_out,
       not_4_out, not_5_out, not_6_out, not_7_out, not_8_out, not_9_out, not_10_out, not_11_out, not_12_out,
       not_13_out, not_15_out, not_17_out, not_19_out, or_3_out, or_4_out, xor_1_out;
  wire [4:0] and_20_out, and_21_out, bit_extender_1_out, bit_extender_2_out, bit_extender_4_out,
       bit_extender_5_out, negator_1_out, or_6_out, or_10_out, subtractor_1_out, subtractor_2_out, xnor_1_out;
  wire [12:0] adder_3_out;
  wire [13:0] and_26_out, xor_2_out;
  wire [14:0] bit_extender_3_out;
  wire [14:14] not_14_out, not_16_out;
  wire [15:0] and_22_out, and_23_out, and_28_out, and_29_out, bit_extender_6_out, bit_extender_7_out,
       bit_extender_8_out, not_20_out, or_7_out, shifter_2_out, shifter_4_out;

  xor xor_1 (xor_1_out, in_3, in_8);
  and and_1 (and_1_out, xor_1_out, and_4_out, nor_1_out);
  not not_1 (not_1_out, and_26_out[13]);
  not not_2 (not_2_out, xor_2_out[13]);
  and and_2 (and_26_out[12], not_1_out, xor_2_out[13]);
  and and_3 (and_26_out[11], not_1_out, not_2_out, xor_2_out[12]);
  assign bit_extender_1_out = {{4{1'b0}}, in_8};  // Bit_Extender bit_extender_1
  assign bit_extender_2_out = {{4{1'b0}}, in_3};  // Bit_Extender bit_extender_2
  and and_4 (and_4_out, xnor_1_out[4], xnor_1_out[3], xnor_1_out[2], xnor_1_out[1], xnor_1_out[0]);
  not not_3 (not_3_out, xor_2_out[12]);
  not not_4 (not_4_out, xor_2_out[11]);
  and and_5 (and_26_out[10], not_1_out, not_2_out, not_3_out, xor_2_out[11]);
  Adder #(.width(5)) adder_1 (.a(in_9), .b(bit_extender_1_out), .out(out_11));  // open: cin, cout
  Adder #(.width(5)) adder_2 (.a(in_4), .b(bit_extender_2_out), .out(out_12));  // open: cin, cout
  assign xnor_1_out = ~(out_12 ^ out_11);  // XNOR_Gate xnor_1, 5 bits wide
  nor nor_1 (nor_1_out, adder_3_out[12], adder_3_out[11], adder_3_out[10], adder_3_out[9], adder_3_out[8], adder_3_out[7], adder_3_out[6], adder_3_out[5], adder_3_out[4], adder_3_out[3], adder_3_out[2], adder_3_out[1], adder_3_out[0]);
  and and_6 (and_6_out, in_7, in_6);
  and and_7 (and_7_out, in_2, in_1);
  and and_8 (and_8_out, in_6, in_1);
  or or_1 (Inf, in_6, in_1);
  not not_5 (not_5_out, xor_2_out[10]);
  and and_9 (and_26_out[9], not_1_out, not_2_out, not_3_out, not_4_out, xor_2_out[10]);
  Adder #(.width(13)) adder_3 (.a(in_10), .b(in_5), .out(adder_3_out));  // open: cin, cout
  and and_10 (and_10_out, in_8, subtractor_1_out[4]);
  not not_6 (not_6_out, xor_1_out);
  and and_11 (and_11_out, in_8, not_6_out);
  or or_2 (sign, and_1_out, and_6_out, and_7_out, and_8_out);
  not not_7 (not_7_out, xor_2_out[8]);
  and and_12 (and_26_out[8], not_1_out, not_2_out, not_3_out, not_4_out, not_5_out, xor_2_out[9]);
  and and_13 (and_13_out, in_3, subtractor_2_out[4]);
  or or_3 (or_3_out, and_10_out, and_13_out);
  nor nor_2 (nor_2_out, subtractor_1_out[4], subtractor_2_out[4]);
  and and_14 (and_14_out, nor_2_out, or_7_out[15]);
  or or_4 (or_4_out, or_3_out, and_14_out);
  and and_15 (and_15_out, xor_1_out, or_4_out);
  or or_5 (out_20, and_11_out, and_15_out);
  and and_16 (underflow, xor_1_out, exponent[4], not_9_out);
  not not_8 (not_8_out, xor_2_out[7]);
  and and_17 (and_26_out[7], not_1_out, not_2_out, not_3_out, not_4_out, not_5_out, not_7_out, xor_2_out[7]);
  Subtractor #(.width(5)) subtractor_1 (.a(in_4), .b(in_9), .out(subtractor_1_out));  // open: bin, bout
  Subtractor #(.width(5)) subtractor_2 (.a(in_9), .b(in_4), .out(subtractor_2_out));  // open: bin, bout
  assign or_6_out = and_21_out | and_20_out;  // OR_Gate or_6, 5 bits wide
  not not_9 (not_9_out, or_6_out[4]);
  not not_10 (not_10_out, xor_2_out[6]);
  and and_18 (and_26_out[6], not_1_out, not_2_out, not_3_out, not_4_out, not_5_out, not_7_out, not_8_out, xor_2_out[6]);
  not not_11 (not_11_out, subtractor_1_out[4]);
  not not_12 (not_12_out, subtractor_2_out[4]);
  assign or_7_out = and_22_out | and_23_out;  // OR_Gate or_7, 16 bits wide
  assign bit_extender_3_out = {{14{out_20}}, out_20};  // Bit_Extender bit_extender_3
  Adder #(.width(5)) adder_4 (.a(or_10_out), .b(or_6_out), .out(exponent));  // open: cin, cout
  and and_19 (and_26_out[5], not_1_out, not_2_out, not_3_out, not_4_out, not_5_out, not_7_out, not_8_out, not_10_out, xor_2_out[5]);
  assign bit_extender_4_out = {{4{not_11_out}}, not_11_out};  // Bit_Extender bit_extender_4
  assign and_20_out = bit_extender_4_out & in_4;  // AND_Gate and_20, 5 bits wide
  assign bit_extender_5_out = {{4{not_12_out}}, not_12_out};  // Bit_Extender bit_extender_5
  assign and_21_out = bit_extender_5_out & in_9;  // AND_Gate and_21, 5 bits wide
  assign bit_extender_6_out = {{15{not_11_out}}, not_11_out};  // Bit_Extender bit_extender_6
  assign and_22_out = bit_extender_6_out & out_17;  // AND_Gate and_22, 16 bits wide
  assign bit_extender_7_out = {{15{not_12_out}}, not_12_out};  // Bit_Extender bit_extender_7
  assign and_23_out = bit_extender_7_out & out_16;  // AND_Gate and_23, 16 bits wide
  assign {and_26_out[13], xor_2_out} = bit_extender_3_out ^ or_7_out[15:1];  // XOR_Gate xor_2, 15 bits wide
  not not_13 (not_13_out, xor_2_out[5]);
  and and_24 (and_26_out[4], not_1_out, not_2_out, not_3_out, not_4_out, not_5_out, not_7_out, not_8_out, not_10_out, not_13_out, xor_2_out[4]);
  not not_14 (not_14_out[14], in_3);
  not not_15 (not_15_out, xor_2_out[4]);
  not not_16 (not_16_out[14], in_8);
  Shifter #(.width(16), .shift("ar")) shifter_1 (
    .in({in_3, not_14_out[14], in_5, 1'b0}), .\dist (subtractor_2_out[3:0]), .out(out_14));
  Adder #(.width(16)) adder_5 (.a({in_8, not_16_out[14], in_10, 1'b0}), .b(out_14), .out(out_16));  // open: cin, cout
  Shifter #(.width(16), .shift("lr")) shifter_2 (.in(or_7_out), .\dist ({3'b000, and_26_out[13]}), .out(shifter_2_out));
  and and_25 (and_26_out[3], not_1_out, not_2_out, not_3_out, not_4_out, not_5_out, not_7_out, not_8_out, not_10_out, not_13_out, not_15_out, xor_2_out[3]);
  Shifter #(.width(16), .shift("ar")) shifter_3 (
    .in({in_8, not_16_out[14], in_10, 1'b0}), .\dist (subtractor_1_out[3:0]), .out(out_15));
  Adder #(.width(16)) adder_6 (.a(out_15), .b({in_3, not_14_out[14], in_5, 1'b0}), .out(out_17));  // open: cin, cout
  Negator #(.width(5)) negator_1 (.in(or_10_out), .out(negator_1_out));
  and and_26 (and_26_out[0], xor_2_out[0], not_17_out, not_17_out, not_19_out, not_15_out, not_13_out, not_10_out, not_8_out, not_7_out, not_5_out, not_4_out, not_3_out, not_2_out, not_1_out);
  not not_17 (not_17_out, xor_2_out[1]);
  not not_18 (not_17_out, xor_2_out[2]);
  not not_19 (not_19_out, xor_2_out[3]);
  and and_27 (and_26_out[2], not_19_out, xor_2_out[2], not_15_out, not_13_out, not_10_out, not_8_out, not_7_out, not_5_out, not_4_out, not_3_out, not_2_out, not_1_out);
  assign out_13 = and_29_out | and_28_out;  // OR_Gate or_8, 16 bits wide
  assign and_28_out = shifter_4_out & not_20_out;  // AND_Gate and_28, 16 bits wide
  assign and_29_out = bit_extender_8_out & shifter_2_out;  // AND_Gate and_29, 16 bits wide
  Shifter #(.width(16)) shifter_4 (.in(or_7_out), .\dist (negator_1_out[3:0]), .out(shifter_4_out));
  and and_30 (and_26_out[1], xor_2_out[1], not_17_out, not_19_out, not_15_out, not_13_out, not_10_out, not_8_out, not_7_out, not_5_out, not_4_out, not_3_out, not_2_out, not_1_out);
  assign not_20_out = ~bit_extender_8_out;  // NOT_Gate not_20, 16 bits wide
  assign bit_extender_8_out = {{15{and_26_out[13]}}, and_26_out[13]};  // Bit_Extender bit_extender_8
  nor nor_3 (or_10_out[4], and_26_out[13], and_26_out[12]);
  nor nor_4 (or_10_out[3], and_26_out[13], and_26_out[12], and_26_out[3], and_26_out[2], and_26_out[1], and_26_out[0], and_31_out);
  nor nor_5 (or_10_out[2], and_31_out, and_26_out[4], and_26_out[5], and_26_out[6], and_26_out[7], and_26_out[12], and_26_out[13]);
  or or_9 (or_10_out[1], and_31_out, and_26_out[2], and_26_out[3], and_26_out[6], and_26_out[7], and_26_out[10], and_26_out[11]);
  or or_10 (or_10_out[0], and_31_out, and_26_out[1], and_26_out[3], and_26_out[5], and_26_out[7], and_26_out[9], and_26_out[11], and_26_out[13]);
  and and_31 (and_31_out, nor_7_out, nor_6_out);
  nor nor_6 (nor_6_out, and_26_out[0], and_26_out[1], and_26_out[2], and_26_out[3], and_26_out[4], and_26_out[5], and_26_out[6]);
  nor nor_7 (nor_7_out, and_26_out[7], and_26_out[8], and_26_out[9], and_26_out[10], and_26_out[11], and_26_out[12], and_26_out[13]);

  // Notes on the sheet:
  //   exponent augment
  //   zero checker
  //   exponent-based
  //   addition or subtraction rail
  //   count leading zeros or ones, as appropriate (set by sign)
  //   sign selector
  //   zero
  //   fraction-based
  //   sign selector
  //   parallel exponent difference
  //   exponent selector
  //   hidden bits augmenter
  //   shifters.
  //   Don't forget the guard bit.
  //   contravariant
  //   try both universes
  //   sort it out later
  //   actual bit addition
  //   such a small part.
  //   left shift (0) or right shift(1)
  //   result fraction. Top two bits are hidden bits
  //   too lazy to strip the guard bit.
  //   one-hot encoding to numerical encodinng
endmodule
