// Logisim project posit_decode.circ as structural Verilog: 1 circuit, main circuit main
module main (
  input  S,
  input  I,
  input  _0,
  input  _1,
  input  _2,
  input  _3,
  input  _4,
  input  _5,
  output out_9,
  output out_10,
  output out_11,
  output out_12,
  output out_13,
  output out_14,
  output out_15,
  output out_16,
  output out_17
);

  wire and_1_out, and_2_out, and_3_out, and_4_out, and_5_out, and_6_out, and_7_out, and_8_out, and_9_out,
       and_10_out, and_11_out, and_12_out, and_13_out, and_14_out, and_15_out, and_16_out, and_17_out,
       and_18_out, and_19_out, and_21_out, and_22_out, and_23_out, and_24_out, and_25_out, and_26_out,
       and_27_out, and_28_out, and_29_out, and_30_out, and_31_out, and_32_out, and_33_out, and_34_out,
       not_1_out, not_2_out, not_3_out, not_4_out, not_5_out, not_6_out, not_7_out, xor_1_out, xor_2_out,
       xor_3_out, xor_4_out, xor_5_out, xor_6_out, xor_7_out;

  xor xor_1 (xor_1_out, I, _1);
  xor xor_2 (xor_2_out, I, _0);
  not not_1 (not_1_out, xor_2_out);
  and and_1 (and_1_out, xor_2_out, _1);
  or or_1 (out_9, and_1_out, and_4_out, and_8_out, and_10_out, and_16_out);
  xor xor_3 (xor_3_out, I, _2);
  not not_2 (not_2_out, xor_1_out);
  and and_2 (and_2_out, xor_1_out, not_1_out);
  and and_3 (and_3_out, xor_2_out, _2);
  and and_4 (and_4_out, and_2_out, _2);
  or or_2 (out_10, and_3_out, and_7_out, and_13_out, and_15_out);
  not not_3 (not_3_out, xor_3_out);
  and and_5 (and_5_out, xor_3_out, not_1_out, not_2_out);
  and and_6 (and_6_out, xor_2_out, _3);
  and and_7 (and_7_out, and_2_out, _3);
  and and_8 (and_8_out, and_5_out, _3);
  xor xor_4 (xor_4_out, I, _3);
  not not_4 (not_4_out, xor_4_out);
  and and_9 (and_9_out, xor_4_out, not_1_out, not_2_out, not_3_out);
  and and_10 (and_10_out, and_9_out, _4);
  or or_3 (out_11, and_6_out, and_12_out, and_18_out);
  and and_11 (and_11_out, xor_2_out, _4);
  and and_12 (and_12_out, and_2_out, _4);
  and and_13 (and_13_out, and_5_out, _4);
  or or_4 (out_12, and_11_out, and_17_out);
  xor xor_5 (xor_5_out, I, _4);
  not not_5 (not_5_out, xor_5_out);
  and and_14 (and_14_out, xor_5_out, not_1_out, not_2_out, not_3_out, not_4_out);
  and and_15 (and_15_out, and_9_out, _5);
  and and_16 (and_16_out, and_14_out, _5);
  and and_17 (and_17_out, and_2_out, _5);
  and and_18 (and_18_out, and_5_out, _5);
  xor xor_6 (xor_6_out, I, _5);
  and and_19 (and_19_out, xor_6_out, not_1_out, not_2_out, not_3_out, not_4_out, not_5_out);
  and and_20 (out_13, xor_2_out, _5);
  xor xor_7 (xor_7_out, S, I);
  and and_21 (and_21_out, not_5_out, not_4_out, not_3_out, not_2_out, not_1_out, not_7_out);
  not not_6 (not_6_out, xor_7_out);
  not not_7 (not_7_out, xor_6_out);
  and and_22 (and_22_out, and_19_out, not_6_out);
  and and_23 (and_23_out, and_14_out, not_6_out);
  and and_24 (and_24_out, and_9_out, not_6_out);
  and and_25 (and_25_out, and_5_out, not_6_out);
  and and_26 (and_26_out, and_2_out, not_6_out);
  and and_27 (and_27_out, xor_2_out, not_6_out);
  and and_28 (and_28_out, xor_2_out, xor_7_out);
  and and_29 (and_29_out, and_2_out, xor_7_out);
  and and_30 (and_30_out, and_5_out, xor_7_out);
  and and_31 (and_31_out, and_9_out, xor_7_out);
  and and_32 (and_32_out, and_14_out, xor_7_out);
  and and_33 (and_33_out, and_19_out, xor_7_out);
  and and_34 (and_34_out, and_21_out, xor_7_out);
  or or_5 (out_14, and_34_out, and_33_out, and_32_out, and_31_out, and_30_out, and_29_out);
  or or_6 (out_15, and_34_out, and_33_out, and_28_out, and_27_out, and_26_out, and_25_out);
  or or_7 (out_16, and_32_out, and_31_out, and_28_out, and_27_out, and_24_out, and_23_out);
  or or_8 (out_17, and_34_out, and_32_out, and_30_out, and_28_out, and_26_out, and_24_out, and_22_out);

  // Notes on the sheet:
  //   shifters
  //   shift value lines (in ascending order)
  //   leading unary cancellation lines
  //   exponent line to binary lookup table
endmodule
