// Logisim project encoder.circ as structural Verilog: 1 circuit, main circuit main
module main (
  input  Inf,
  input  zero,
  input  sign,
  input  [3:0] exp,
  input  [4:0] frac,
  input  gd,
  input  sm,
  output [3:0] out_8,
  output [2:0] out_9,
  output [2:0] out_10,
  output [7:0] out_11,
  output [7:0] out_12,
  output [7:0] out_13
);

  wire and_1_out, and_2_out, or_1_out;
  wire [0:0] multiplexer_3_out_2;
  wire [2:0] bit_extender_1_out, negator_1_out;
  wire [6:0] multiplexer_3_out;
  wire [7:0] adder_1_out, bit_extender_2_out;
  wire [7:6] xor_1_out;

  Subtractor #(.width(4)) subtractor_1 (.a(exp), .b(4'b0111), .out(out_8));  // open: bin, bout
  Negator #(.width(3)) negator_1 (.in(out_8[2:0]), .out(negator_1_out));
  xor xor_1 (xor_1_out[6], out_8[3], sign);
  Multiplexer #(.width(3)) multiplexer_1 (
    .in0(out_8[2:0]), .in1(negator_1_out), .out(out_10), .sel(out_8[3]));  // open: en
  assign bit_extender_1_out = {{2{1'b0}}, out_8[3]};  // Bit_Extender bit_extender_1
  Multiplexer #(.select(2), .width(8)) multiplexer_2 (
    .in0(adder_1_out), .in1({8{1'b0}}), .in2(8'h80), .out(out_13), .sel({Inf, zero}));  // open: in3, en
  not not_1 (xor_1_out[7], xor_1_out[6]);
  Subtractor #(.width(3)) subtractor_2 (.a(out_10), .b(bit_extender_1_out), .out(out_9));  // open: bin, bout
  Shifter #(.shift("ar")) shifter_1 (.in({xor_1_out, frac, gd}), .\dist (out_9), .out(out_11));
  Shifter #(.shift("lr")) shifter_2 (.in({xor_1_out, frac, gd}), .\dist (out_9), .out(out_12));
  Multiplexer #(.width(8)) multiplexer_3 (
    .in0(out_11), .in1(out_12), .out({multiplexer_3_out, multiplexer_3_out_2[0]}), .sel(xor_1_out[6]));  // open: en
  Adder adder_1 (.a({sign, multiplexer_3_out}), .b(bit_extender_2_out), .out(adder_1_out));  // open: cin, cout
  assign bit_extender_2_out = {{7{1'b0}}, or_1_out};  // Bit_Extender bit_extender_2
  and and_1 (and_1_out, multiplexer_3_out[0], multiplexer_3_out_2[0]);
  and and_2 (and_2_out, multiplexer_3_out_2[0], sm);
  or or_1 (or_1_out, and_1_out, and_2_out);
endmodule
