// Logisim project encoder2.circ as structural Verilog: 1 circuit, main circuit main
module main (
  input  Inf,
  input  zero,
  input  sign,
  input  [3:0] regime,
  input  [4:0] frac,
  input  gd,
  input  sm,
  output [3:0] out_8,
  output [2:0] out_9,
  output [2:0] out_10,
  output [7:0] out_11
);

  wire and_1_out, and_2_out, and_3_out, and_4_out, and_5_out, and_6_out, and_7_out, and_9_out, and_10_out,
       and_11_out, and_12_out, and_13_out, and_14_out, and_15_out, and_16_out, and_17_out, and_18_out,
       and_19_out, and_20_out, and_21_out, and_22_out, and_23_out, and_24_out, and_25_out, and_26_out,
       and_27_out, and_28_out, and_29_out, and_30_out, and_31_out, and_32_out, and_33_out, and_34_out,
       and_35_out, and_36_out, and_37_out, and_38_out, and_39_out, and_40_out, and_41_out, and_42_out,
       and_43_out, and_44_out, and_45_out, and_46_out, and_47_out, and_48_out, and_49_out, and_50_out,
       and_51_out, not_1_out, not_2_out, not_3_out, not_4_out, or_1_out, or_2_out, or_4_out, or_6_out,
       or_7_out, or_9_out, or_11_out, or_14_out, or_15_out, or_16_out, or_17_out, or_18_out, or_19_out,
       or_20_out, or_21_out, xor_1_out;
  wire [2:0] bit_extender_1_out, negator_1_out;
  wire [6:0] or_13_out;
  wire [7:0] adder_1_out, bit_extender_2_out;

  Subtractor #(.width(4)) subtractor_1 (.a(regime), .b(4'b0111), .out(out_8));  // open: bin, bout
  Multiplexer #(.width(3)) multiplexer_1 (
    .in0(out_8[2:0]), .in1(negator_1_out), .out(out_9), .sel(out_8[3]));  // open: en
  Negator #(.width(3)) negator_1 (.in(out_8[2:0]), .out(negator_1_out));
  xor xor_1 (xor_1_out, out_8[3], sign);
  assign bit_extender_1_out = {{2{1'b0}}, out_8[3]};  // Bit_Extender bit_extender_1
  Multiplexer #(.select(2), .width(8)) multiplexer_2 (
    .in0(adder_1_out), .in1({8{1'b0}}), .in2(8'h80), .out(out_11), .sel({Inf, zero}));  // open: in3, en
  not not_1 (not_1_out, xor_1_out);
  Subtractor #(.width(3)) subtractor_2 (.a(out_9), .b(bit_extender_1_out), .out(out_10));  // open: bin, bout
  and and_1 (and_1_out, not_2_out, not_3_out, not_4_out);
  not not_2 (not_2_out, out_10[0]);
  not not_3 (not_3_out, out_10[1]);
  not not_4 (not_4_out, out_10[2]);
  and and_2 (and_2_out, out_10[0], not_3_out, not_4_out);
  and and_3 (and_3_out, not_2_out, out_10[1], not_4_out);
  and and_4 (and_4_out, not_2_out, not_3_out, out_10[2]);
  and and_5 (and_5_out, out_10[0], out_10[1], not_4_out);
  and and_6 (and_6_out, out_10[0], not_3_out, out_10[2]);
  and and_7 (and_7_out, not_2_out, out_10[1], out_10[2]);
  or or_1 (or_1_out, and_7_out, and_6_out, and_4_out, and_5_out, and_3_out, and_2_out, and_1_out);
  or or_2 (or_2_out, and_7_out, and_6_out, and_4_out, and_5_out, and_3_out, and_2_out);
  and and_8 (or_13_out[6], or_1_out, not_1_out);
  Adder adder_1 (.a({sign, or_13_out}), .b(bit_extender_2_out), .out(adder_1_out));  // open: cin, cout
  assign bit_extender_2_out = {{7{1'b0}}, or_6_out};  // Bit_Extender bit_extender_2
  and and_9 (and_9_out, and_1_out, xor_1_out);
  and and_10 (and_10_out, or_2_out, not_1_out);
  or or_3 (or_13_out[5], and_10_out, and_9_out);
  or or_4 (or_4_out, and_7_out, and_6_out, and_4_out, and_5_out, and_3_out);
  and and_11 (and_11_out, or_4_out, not_1_out);
  or or_5 (or_13_out[4], and_11_out, and_15_out, and_14_out);
  and and_12 (and_12_out, or_13_out[0], or_14_out);
  and and_13 (and_13_out, or_14_out, or_16_out);
  or or_6 (or_6_out, and_12_out, and_13_out);
  and and_14 (and_14_out, and_1_out, frac[4]);
  and and_15 (and_15_out, and_2_out, xor_1_out);
  and and_16 (and_16_out, and_3_out, xor_1_out);
  or or_7 (or_7_out, and_7_out, and_6_out, and_4_out, and_5_out);
  and and_17 (and_17_out, or_7_out, not_1_out);
  or or_8 (or_13_out[3], and_17_out, and_16_out, and_19_out, and_18_out);
  and and_18 (and_18_out, and_1_out, frac[3]);
  and and_19 (and_19_out, and_2_out, frac[4]);
  and and_20 (and_20_out, and_5_out, xor_1_out);
  or or_9 (or_9_out, and_7_out, and_6_out, and_4_out);
  and and_21 (and_21_out, or_9_out, not_1_out);
  or or_10 (or_13_out[2], and_21_out, and_20_out, and_24_out, and_23_out, and_22_out);
  and and_22 (and_22_out, and_1_out, frac[2]);
  and and_23 (and_23_out, and_2_out, frac[3]);
  and and_24 (and_24_out, and_3_out, frac[4]);
  or or_11 (or_11_out, and_7_out, and_6_out);
  and and_25 (and_25_out, or_11_out, not_1_out);
  or or_12 (or_13_out[1], and_25_out, and_28_out, and_27_out, and_26_out, and_30_out, and_29_out);
  and and_26 (and_26_out, and_3_out, frac[3]);
  and and_27 (and_27_out, and_5_out, frac[4]);
  and and_28 (and_28_out, and_4_out, xor_1_out);
  and and_29 (and_29_out, and_1_out, frac[1]);
  and and_30 (and_30_out, and_2_out, frac[2]);
  and and_31 (and_31_out, and_4_out, frac[4]);
  and and_32 (and_32_out, and_6_out, xor_1_out);
  and and_33 (and_33_out, and_7_out, not_1_out);
  or or_13 (or_13_out[0], and_33_out, and_32_out, and_31_out, and_35_out, and_34_out, and_37_out, and_36_out);
  and and_34 (and_34_out, and_3_out, frac[2]);
  and and_35 (and_35_out, and_5_out, frac[3]);
  and and_36 (and_36_out, and_1_out, frac[0]);
  and and_37 (and_37_out, and_2_out, frac[1]);
  and and_38 (and_38_out, and_6_out, frac[4]);
  and and_39 (and_39_out, and_7_out, xor_1_out);
  or or_14 (or_14_out, and_39_out, and_38_out, and_42_out, and_41_out, and_40_out, and_44_out, and_43_out);
  and and_40 (and_40_out, and_3_out, frac[1]);
  and and_41 (and_41_out, and_5_out, frac[2]);
  and and_42 (and_42_out, and_4_out, frac[3]);
  and and_43 (and_43_out, and_1_out, gd);
  and and_44 (and_44_out, and_2_out, frac[0]);
  or or_15 (or_15_out, gd, sm);
  and and_45 (and_45_out, and_2_out, or_15_out);
  and and_46 (and_46_out, and_1_out, sm);
  or or_16 (or_16_out, and_46_out, and_45_out, and_47_out, and_48_out, and_49_out, and_50_out, and_51_out);
  or or_17 (or_17_out, frac[0], gd, sm);
  and and_47 (and_47_out, and_3_out, or_17_out);
  or or_18 (or_18_out, frac[1], frac[0], gd, sm);
  and and_48 (and_48_out, and_5_out, or_18_out);
  or or_19 (or_19_out, frac[2], frac[1], frac[0], gd, sm);
  and and_49 (and_49_out, and_4_out, or_19_out);
  or or_20 (or_20_out, frac[3], frac[2], frac[1], frac[0], gd, sm);
  and and_50 (and_50_out, and_6_out, or_20_out);
  or or_21 (or_21_out, frac[4], frac[3], frac[2], frac[1], frac[0], gd, sm);
  and and_51 (and_51_out, and_7_out, or_21_out);

  // Notes on the sheet:
  //   regime -> regimeshift
  //   would be nice to find a better method
  //   regime shift -> one-hot shifts
  //   shift encoding
  //   summary_bit accumulation
endmodule
