// Logisim project posit_mult.circ as structural Verilog: 1 circuit, main circuit main
module main (
  input  in_1,
  input  [4:0] in_2,
  input  in_3,
  input  [4:0] in_4,
  output [4:0] out_5,
  output [4:0] out_6,
  output [12:0] out_7,
  output [12:0] out_8,
  output [12:0] out_9,
  output [12:0] out_10,
  output sign_bit,
  output exp_augment,
  output [9:0] out_13
);

  wire and_2_out, and_4_out, and_5_out, and_6_out, and_7_out, and_8_out, and_9_out, and_10_out, and_13_out,
       and_15_out, and_16_out, and_17_out, and_18_out, and_19_out, and_20_out, and_21_out, and_25_out,
       not_1_out, not_2_out, not_3_out, or_1_out, or_6_out;
  wire [4:0] negator_1_out, negator_2_out;
  wire [9:0] and_23_out, and_24_out, bit_extender_1_out, bit_extender_2_out;
  wire [12:5] and_22_out;
  wire [12:10] and_26_out;

  or or_1 (or_1_out, negator_1_out[4], negator_1_out[3], negator_1_out[2], negator_1_out[1], negator_1_out[0]);
  and and_1 (out_9[10], in_3, negator_1_out[4]);
  and and_2 (and_2_out, in_2[4], not_1_out);
  and and_3 (out_9[12], or_1_out, in_3);
  or or_2 (out_9[9], and_2_out, and_5_out);
  Negator #(.width(5)) negator_1 (.in(in_2), .out(negator_1_out));
  and and_4 (and_4_out, in_3, negator_1_out[2]);
  and and_5 (and_5_out, in_3, negator_1_out[3]);
  and and_6 (and_6_out, in_2[3], not_1_out);
  and and_7 (and_7_out, in_2[2], not_1_out);
  or or_3 (out_9[7], and_7_out, and_9_out);
  or or_4 (out_9[8], and_6_out, and_4_out);
  and and_8 (and_8_out, in_3, negator_1_out[0]);
  and and_9 (and_9_out, in_3, negator_1_out[1]);
  and and_10 (and_10_out, in_2[1], not_1_out);
  and and_11 (out_9[5], in_2[0], not_1_out);
  or or_5 (out_9[6], and_10_out, and_8_out);
  not not_1 (not_1_out, in_3);
  xor xor_1 (exp_augment, sign_bit, out_10[11]);
  Multiplier #(.width(5)) multiplier_1 (.a(in_4), .b(in_2), .out(out_6), .cout(out_5));  // open: cin
  not not_2 (not_2_out, exp_augment);
  assign bit_extender_1_out = {{9{not_2_out}}, not_2_out};  // Bit_Extender bit_extender_1
  assign bit_extender_2_out = {{9{exp_augment}}, exp_augment};  // Bit_Extender bit_extender_2
  Negator #(.width(5)) negator_2 (.in(in_4), .out(negator_2_out));
  or or_6 (or_6_out, negator_2_out[0], negator_2_out[1], negator_2_out[2], negator_2_out[3], negator_2_out[4]);
  and and_12 (and_22_out[12], or_6_out, in_1);
  Adder #(.width(13)) adder_1 (
    .a({3'b000, out_5, out_6}), .b({{2{out_9[12]}}, out_9[10:5], {5{1'b0}}}), .out(out_8));  // open: cin, cout
  and and_13 (and_13_out, in_1, negator_2_out[3]);
  and and_14 (and_22_out[10], in_1, negator_2_out[4]);
  and and_15 (and_15_out, in_4[4], not_3_out);
  and and_16 (and_16_out, in_4[3], not_3_out);
  or or_7 (and_22_out[8], and_16_out, and_17_out);
  or or_8 (and_22_out[9], and_15_out, and_13_out);
  and and_17 (and_17_out, in_1, negator_2_out[2]);
  and and_18 (and_18_out, in_1, negator_2_out[1]);
  and and_19 (and_19_out, in_4[2], not_3_out);
  and and_20 (and_20_out, in_4[1], not_3_out);
  or or_9 (and_22_out[7], and_19_out, and_18_out);
  or or_10 (and_22_out[6], and_20_out, and_21_out);
  not not_3 (not_3_out, in_1);
  and and_21 (and_21_out, in_1, negator_2_out[0]);
  and and_22 (and_22_out[5], in_4[0], not_3_out);
  or or_11 (and_26_out[12], and_25_out, sign_bit);
  Adder #(.width(13)) adder_2 (
    .a({{2{and_22_out[12]}}, and_22_out[10:5], {5{1'b0}}}), .b(out_8), .out(out_7));  // open: cin, cout
  assign and_23_out = out_10[9:0] & bit_extender_1_out;  // AND_Gate and_23, 10 bits wide
  assign and_24_out = out_10[10:1] & bit_extender_2_out;  // AND_Gate and_24, 10 bits wide
  and and_25 (and_25_out, in_1, in_3);
  assign out_13 = and_23_out | and_24_out;  // OR_Gate or_12, 10 bits wide
  and and_26 (and_26_out[10], not_3_out, not_1_out);
  xor xor_2 (sign_bit, in_1, in_3);
  Adder #(.width(13)) adder_3 (
    .a({and_26_out[12], sign_bit, and_26_out[10], {10{1'b0}}}), .b(out_7), .out(out_10));  // open: cin, cout

  assign {out_9[11], out_9[4:0]} = {out_9[12], {5{1'b0}}};

  // Notes on the sheet:
  //   Left Frac/Right Hidden preparer
  //   core fraction multiplier
  //   concatenation
  //   shift selector
  //   Right Frac/Left Hidden preparer
  //   ignore top 3 bits
  //   ignore top 2 bits
  //   Hidden Bit Unit
  //   fraction
endmodule
