// Logisim project regimeshifter.circ as structural Verilog: 1 circuit, main circuit main
module main (
  input  I,
  input  _0,
  input  _1,
  input  _2,
  input  _3,
  input  _4,
  input  _5,
  input  _6,
  output out_9,
  output out_10,
  output out_11,
  output out_12,
  output out_13,
  output out_14
);

  wire and_1_out, and_2_out, and_3_out, and_4_out, and_5_out, and_6_out, and_7_out, and_8_out, and_9_out,
       and_10_out, and_11_out, and_12_out, and_13_out, and_14_out, and_15_out, and_16_out, and_17_out,
       and_18_out, and_19_out, and_20_out, and_21_out, and_22_out, and_23_out, and_25_out, and_26_out,
       not_1_out, not_2_out, not_3_out, not_4_out, not_5_out, xor_1_out, xor_2_out, xor_3_out, xor_4_out,
       xor_5_out, xor_6_out;

  xor xor_1 (xor_1_out, I, _1);
  xor xor_2 (xor_2_out, I, _0);
  not not_1 (not_1_out, xor_2_out);
  and and_1 (and_1_out, xor_2_out, _1);
  or or_1 (out_9, and_1_out, and_4_out, and_8_out, and_10_out, and_16_out, and_21_out);
  xor xor_3 (xor_3_out, I, _2);
  not not_2 (not_2_out, xor_1_out);
  and and_2 (and_2_out, xor_1_out, not_1_out);
  and and_3 (and_3_out, xor_2_out, _2);
  and and_4 (and_4_out, and_2_out, _2);
  or or_2 (out_10, and_3_out, and_7_out, and_13_out, and_15_out, and_23_out);
  not not_3 (not_3_out, xor_3_out);
  and and_5 (and_5_out, xor_3_out, not_1_out, not_2_out);
  and and_6 (and_6_out, xor_2_out, _3);
  and and_7 (and_7_out, and_2_out, _3);
  and and_8 (and_8_out, and_5_out, _3);
  xor xor_4 (xor_4_out, I, _3);
  not not_4 (not_4_out, xor_4_out);
  and and_9 (and_9_out, xor_4_out, not_1_out, not_2_out, not_3_out);
  and and_10 (and_10_out, and_9_out, _4);
  or or_3 (out_11, and_6_out, and_12_out, and_18_out, and_22_out);
  and and_11 (and_11_out, xor_2_out, _4);
  and and_12 (and_12_out, and_2_out, _4);
  and and_13 (and_13_out, and_5_out, _4);
  or or_4 (out_12, and_11_out, and_17_out, and_26_out);
  xor xor_5 (xor_5_out, I, _4);
  not not_5 (not_5_out, xor_5_out);
  and and_14 (and_14_out, xor_5_out, not_1_out, not_2_out, not_3_out, not_4_out);
  and and_15 (and_15_out, and_9_out, _5);
  and and_16 (and_16_out, and_14_out, _5);
  and and_17 (and_17_out, and_2_out, _5);
  and and_18 (and_18_out, and_5_out, _5);
  xor xor_6 (xor_6_out, I, _5);
  and and_19 (and_19_out, xor_6_out, not_1_out, not_2_out, not_3_out, not_4_out, not_5_out);
  and and_20 (and_20_out, xor_2_out, _5);
  and and_21 (and_21_out, and_19_out, _6);
  or or_5 (out_13, and_20_out, and_25_out);
  and and_22 (and_22_out, and_9_out, _6);
  and and_23 (and_23_out, and_14_out, _6);
  and and_24 (out_14, xor_2_out, _6);
  and and_25 (and_25_out, and_2_out, _6);
  and and_26 (and_26_out, and_5_out, _6);
endmodule
